// Logisim project dtapath_without_ControlUnit.circ as structural Verilog: 5 circuits, main circuit main
module main (
  input  [15:0] in_1,
  input  [15:0] in_2,
  input  in_3,
  input  [3:0] in_4,
  input  [3:0] in_5,
  input  [3:0] in_6,
  input  [15:0] in_7,
  input  in_8,
  input  in_9,
  output [15:0] out_10,
  output [15:0] out_11
);

  wire clock_1_out, clock_2_out;

  _1bit_ALU u_1bit_alu_1 ();  // open: Cout, ALU_Select, Result, A, B, Cin
  Clock clock_1 (.out(clock_1_out));
  Register #(.width(16)) register_1 (.D(in_1), .en(in_3), .Q(in_2), .clk(clock_1_out), .clr(1'b0));
  _16BitIn_ALU u_16bitin_alu_1 ();  // open: in_1, in_2, in_3, in_4, Result, out_6, Zero_flag, Over_Flow
  Register_File register_file_1 (
    .RS(in_4), .RT(in_5), .RD(in_6), .Write_Data(in_7), .Read_Data_1(out_10), .Read_Data_2(out_11),
    .WC(in_9), .CLK(clock_2_out), .CLR(in_8));
  Clock clock_2 (.out(clock_2_out));
endmodule

module _16BitIn_ALU (
  input  in_1,
  input  [15:0] in_2,
  input  [1:0] in_3,
  input  [15:0] in_4,
  output Over_Flow,
  output out_6,
  output [15:0] Result,
  output Zero_flag
);

  wire n1bit_alu_1_cout, n1bit_alu_2_cout, n1bit_alu_3_cout, n1bit_alu_4_cout, n1bit_alu_5_cout,
       n1bit_alu_6_cout, n1bit_alu_7_cout, n1bit_alu_8_cout, n1bit_alu_9_cout, n1bit_alu_10_cout,
       n1bit_alu_11_cout, n1bit_alu_12_cout, n1bit_alu_13_cout, n1bit_alu_14_cout, n1bit_alu_15_cout;

  Comparator #(.width(16)) comparator_1 (.a(in_4), .b(in_2), .eq(Zero_flag));  // open: gt, lt
  _1bit_ALU u_1bit_alu_1 (
    .Cout(n1bit_alu_1_cout), .ALU_Select(in_3), .Result(Result[0]), .A(in_2[0]), .B(in_4[0]), .Cin(in_1));
  _1bit_ALU u_1bit_alu_2 (
    .Cout(n1bit_alu_2_cout), .ALU_Select(in_3), .Result(Result[1]), .A(in_2[1]), .B(in_4[1]),
    .Cin(n1bit_alu_1_cout));
  _1bit_ALU u_1bit_alu_3 (
    .Cout(n1bit_alu_3_cout), .ALU_Select(in_3), .Result(Result[2]), .A(in_2[2]), .B(in_4[2]),
    .Cin(n1bit_alu_2_cout));
  _1bit_ALU u_1bit_alu_4 (
    .Cout(n1bit_alu_4_cout), .ALU_Select(in_3), .Result(Result[3]), .A(in_2[3]), .B(in_4[3]),
    .Cin(n1bit_alu_3_cout));
  _1bit_ALU u_1bit_alu_5 (
    .Cout(n1bit_alu_5_cout), .ALU_Select(in_3), .Result(Result[4]), .A(in_2[4]), .B(in_4[4]),
    .Cin(n1bit_alu_4_cout));
  _1bit_ALU u_1bit_alu_6 (
    .Cout(n1bit_alu_6_cout), .ALU_Select(in_3), .Result(Result[5]), .A(in_2[5]), .B(in_4[5]),
    .Cin(n1bit_alu_5_cout));
  _1bit_ALU u_1bit_alu_7 (
    .Cout(n1bit_alu_7_cout), .ALU_Select(in_3), .Result(Result[6]), .A(in_2[6]), .B(in_4[6]),
    .Cin(n1bit_alu_6_cout));
  _1bit_ALU u_1bit_alu_8 (
    .Cout(n1bit_alu_8_cout), .ALU_Select(in_3), .Result(Result[7]), .A(in_2[7]), .B(in_4[7]),
    .Cin(n1bit_alu_7_cout));
  _1bit_ALU u_1bit_alu_9 (
    .Cout(n1bit_alu_9_cout), .ALU_Select(in_3), .Result(Result[8]), .A(in_2[8]), .B(in_4[8]),
    .Cin(n1bit_alu_8_cout));
  _1bit_ALU u_1bit_alu_10 (
    .Cout(n1bit_alu_10_cout), .ALU_Select(in_3), .Result(Result[9]), .A(in_2[9]), .B(in_4[9]),
    .Cin(n1bit_alu_9_cout));
  _1bit_ALU u_1bit_alu_11 (
    .Cout(n1bit_alu_11_cout), .ALU_Select(in_3), .Result(Result[10]), .A(in_2[10]), .B(in_4[10]),
    .Cin(n1bit_alu_10_cout));
  _1bit_ALU u_1bit_alu_12 (
    .Cout(n1bit_alu_12_cout), .ALU_Select(in_3), .Result(Result[11]), .A(in_2[11]), .B(in_4[11]),
    .Cin(n1bit_alu_11_cout));
  _1bit_ALU u_1bit_alu_13 (
    .Cout(n1bit_alu_13_cout), .ALU_Select(in_3), .Result(Result[12]), .A(in_2[12]), .B(in_4[12]),
    .Cin(n1bit_alu_12_cout));
  _1bit_ALU u_1bit_alu_14 (
    .Cout(n1bit_alu_14_cout), .ALU_Select(in_3), .Result(Result[13]), .A(in_2[13]), .B(in_4[13]),
    .Cin(n1bit_alu_13_cout));
  _1bit_ALU u_1bit_alu_15 (
    .Cout(n1bit_alu_15_cout), .ALU_Select(in_3), .Result(Result[14]), .A(in_2[14]), .B(in_4[14]),
    .Cin(n1bit_alu_14_cout));
  _1bit_ALU u_1bit_alu_16 (
    .Cout(out_6), .ALU_Select(in_3), .Result(Result[15]), .A(in_2[15]), .B(in_4[15]), .Cin(n1bit_alu_15_cout));
  xor xor_1 (Over_Flow, n1bit_alu_15_cout, out_6);
endmodule

module _1bit_ALU (
  input  A,
  input  B,
  input  Cin,
  input  [1:0] ALU_Select,
  output Result,
  output Cout
);

  wire adder_1_out, and_1_out, multiplexer_1_out, not_1_out, or_1_out;

  not not_1 (not_1_out, B);
  Multiplexer #(.enable("false")) multiplexer_1 (
    .in0(B), .in1(not_1_out), .out(multiplexer_1_out), .sel(ALU_Select[0]));
  and and_1 (and_1_out, A, B);
  or or_1 (or_1_out, A, B);
  Adder #(.width(1)) adder_1 (.a(A), .b(multiplexer_1_out), .out(adder_1_out), .cin(Cin), .cout(Cout));
  Multiplexer #(.select(2), .enable("false")) multiplexer_2 (
    .in0(and_1_out), .in1(or_1_out), .in2(adder_1_out), .in3(adder_1_out), .out(Result), .sel(ALU_Select));
endmodule

module Register_File (
  input  [3:0] RS,
  input  [3:0] RT,
  input  [3:0] RD,
  input  [15:0] Write_Data,
  input  WC,
  input  CLK,
  input  CLR,
  output [15:0] Read_Data_1,
  output [15:0] Read_Data_2
);

  wire and_1_out, and_2_out, and_3_out, and_4_out, and_5_out, and_6_out, and_7_out, and_8_out, and_9_out,
       and_10_out, and_11_out, and_12_out, and_13_out, and_14_out, and_15_out, and_16_out, decoder_1_out0,
       decoder_1_out1, decoder_1_out2, decoder_1_out3, decoder_1_out4, decoder_1_out5, decoder_1_out6,
       decoder_1_out7, decoder_1_out8, decoder_1_out9, decoder_1_out10, decoder_1_out11, decoder_1_out12,
       decoder_1_out13, decoder_1_out14, decoder_1_out15;
  wire [15:0] register_1_q, register_2_q, register_3_q, register_4_q, register_5_q, register_6_q,
       register_7_q, register_8_q, register_9_q, register_10_q, register_11_q, register_12_q, register_13_q,
       register_14_q, register_15_q, register_16_q;

  Decoder #(.select(4)) decoder_1 (
    .out0(decoder_1_out0), .out1(decoder_1_out1), .out2(decoder_1_out2), .out3(decoder_1_out3),
    .out4(decoder_1_out4), .out5(decoder_1_out5), .out6(decoder_1_out6), .out7(decoder_1_out7),
    .out8(decoder_1_out8), .out9(decoder_1_out9), .out10(decoder_1_out10), .out11(decoder_1_out11),
    .out12(decoder_1_out12), .out13(decoder_1_out13), .out14(decoder_1_out14), .out15(decoder_1_out15),
    .sel(RD), .en(1'b1));
  and and_1 (and_1_out, WC, decoder_1_out0);
  and and_2 (and_2_out, WC, decoder_1_out1);
  and and_3 (and_3_out, WC, decoder_1_out2);
  and and_4 (and_4_out, WC, decoder_1_out3);
  and and_5 (and_5_out, WC, decoder_1_out4);
  and and_6 (and_6_out, WC, decoder_1_out5);
  and and_7 (and_7_out, WC, decoder_1_out6);
  and and_8 (and_8_out, WC, decoder_1_out7);
  Register #(.width(16)) register_1 (.D(Write_Data), .en(and_1_out), .Q(register_1_q), .clk(CLK), .clr(CLR));
  Register #(.width(16)) register_2 (.D(Write_Data), .en(and_2_out), .Q(register_2_q), .clk(CLK), .clr(CLR));
  Register #(.width(16)) register_3 (.D(Write_Data), .en(and_3_out), .Q(register_3_q), .clk(CLK), .clr(CLR));
  Register #(.width(16)) register_4 (.D(Write_Data), .en(and_4_out), .Q(register_4_q), .clk(CLK), .clr(CLR));
  Register #(.width(16)) register_5 (.D(Write_Data), .en(and_5_out), .Q(register_5_q), .clk(CLK), .clr(CLR));
  Register #(.width(16)) register_6 (.D(Write_Data), .en(and_6_out), .Q(register_6_q), .clk(CLK), .clr(CLR));
  Register #(.width(16)) register_7 (.D(Write_Data), .en(and_7_out), .Q(register_7_q), .clk(CLK), .clr(CLR));
  Register #(.width(16)) register_8 (.D(Write_Data), .en(and_8_out), .Q(register_8_q), .clk(CLK), .clr(CLR));
  and and_9 (and_9_out, WC, decoder_1_out8);
  and and_10 (and_10_out, WC, decoder_1_out9);
  and and_11 (and_11_out, WC, decoder_1_out10);
  and and_12 (and_12_out, WC, decoder_1_out11);
  and and_13 (and_13_out, WC, decoder_1_out12);
  and and_14 (and_14_out, WC, decoder_1_out13);
  and and_15 (and_15_out, WC, decoder_1_out14);
  Register #(.width(16)) register_9 (.D(Write_Data), .en(and_9_out), .Q(register_9_q), .clk(CLK), .clr(CLR));
  Register #(.width(16)) register_10 (.D(Write_Data), .en(and_10_out), .Q(register_10_q), .clk(CLK), .clr(CLR));
  Register #(.width(16)) register_11 (.D(Write_Data), .en(and_11_out), .Q(register_11_q), .clk(CLK), .clr(CLR));
  Register #(.width(16)) register_12 (.D(Write_Data), .en(and_12_out), .Q(register_12_q), .clk(CLK), .clr(CLR));
  Register #(.width(16)) register_13 (.D(Write_Data), .en(and_13_out), .Q(register_13_q), .clk(CLK), .clr(CLR));
  Register #(.width(16)) register_14 (.D(Write_Data), .en(and_14_out), .Q(register_14_q), .clk(CLK), .clr(CLR));
  Register #(.width(16)) register_15 (.D(Write_Data), .en(and_15_out), .Q(register_15_q), .clk(CLK), .clr(CLR));
  Register #(.width(16)) register_16 (.D(Write_Data), .en(and_16_out), .Q(register_16_q), .clk(CLK), .clr(CLR));
  and and_16 (and_16_out, WC, decoder_1_out15);
  Multiplexer #(.select(4), .width(16)) multiplexer_1 (
    .in0(register_1_q), .in1(register_2_q), .in2(register_3_q), .in3(register_4_q), .in4(register_5_q),
    .in5(register_6_q), .in6(register_7_q), .in7(register_8_q), .in8(register_9_q), .in9(register_10_q),
    .in10(register_11_q), .in11(register_12_q), .in12(register_13_q), .in13(register_14_q),
    .in14(register_15_q), .in15(register_16_q), .out(Read_Data_1), .sel(RS), .en(1'b1));
  Multiplexer #(.select(4), .width(16)) multiplexer_2 (
    .in0(register_1_q), .in1(register_2_q), .in2(register_3_q), .in3(register_4_q), .in4(register_5_q),
    .in5(register_6_q), .in6(register_7_q), .in7(register_8_q), .in8(register_9_q), .in9(register_10_q),
    .in10(register_11_q), .in11(register_12_q), .in12(register_13_q), .in13(register_14_q),
    .in14(register_15_q), .in15(register_16_q), .out(Read_Data_2), .sel(RT), .en(1'b1));
endmodule

module datapath (
  input  Cin,
  input  ALU_Src,
  input  Reg_dest,
  input  [1:0] in_4
);

  wire [3:0] multiplexer_1_out;
  wire [15:0] adder_1_out, bit_extender_1_out, multiplexer_2_out, multiplexer_3_out, n16bitin_alu_1_result,
       ram_1_data, register_1_q, register_file_1_read_data_1, register_file_1_read_data_2, rom_1_data;

  Register #(.width(16)) register_1 (.D(adder_1_out), .Q(register_1_q));  // open: en, clk, clr
  Adder #(.width(16)) adder_1 (.a(16'h1), .b(register_1_q), .out(adder_1_out), .cin(1'b0));  // open: cout
  ROM #(.addrWidth(16), .dataWidth(16)) rom_1 (.addr(register_1_q), .data(rom_1_data));  // open: sel
  Multiplexer #(.width(4), .enable("false")) multiplexer_1 (
    .in0(rom_1_data[7:4]), .in1(rom_1_data[3:0]), .out(multiplexer_1_out), .sel(Reg_dest));
  Register_File register_file_1 (
    .RS(rom_1_data[11:8]), .RT(rom_1_data[7:4]), .RD(multiplexer_1_out), .Write_Data(multiplexer_3_out),
    .Read_Data_1(register_file_1_read_data_1), .Read_Data_2(register_file_1_read_data_2));  // open: WC, CLK, CLR
  assign bit_extender_1_out = {{12{1'b0}}, rom_1_data[3:0]};  // Bit_Extender bit_extender_1
  Multiplexer #(.width(16), .enable("false")) multiplexer_2 (
    .in0(register_file_1_read_data_2), .in1(bit_extender_1_out), .out(multiplexer_2_out), .sel(ALU_Src));
  _16BitIn_ALU u_16bitin_alu_1 (
    .in_1(Cin), .in_2(register_file_1_read_data_1), .in_3(in_4), .in_4(multiplexer_2_out),
    .Result(n16bitin_alu_1_result));  // open: out_6, Zero_flag, Over_Flow
  Multiplexer #(.width(16), .enable("false")) multiplexer_3 (
    .in0(n16bitin_alu_1_result), .in1(ram_1_data), .out(multiplexer_3_out));  // open: sel
  RAM #(.addrWidth(16), .dataWidth(16)) ram_1 (
    .addr(n16bitin_alu_1_result), .data(ram_1_data));  // open: sel, clk, ld, clr
endmodule
